# Fritzing sketch GSM_activation_fritizing (saved by Fritzing 0.9.2b)
breadboards: 1

parts:
  Componente1 = Arduino GSM Shield
  LED1 = LED - 5mm [color="Red (633nm)" package="5 mm [THT]"]
  R1 = Resistor [tolerance=±5% resistance=220 package=THT]
  U1 = RELAY [package=relay-g5q]
  D1 = Zener Diode [part_number=1N4732A breakdown_voltage=3.6V package="300 mil [THT]"]
  BC547 = PNP-Transistor [package="SOT-23 [SMD]"]

nets:
  N1: Componente1.AGND, BC547.2
  N2: Componente1.SCK/D13, R1.Pin_1
  N3: Componente1.5V, U1.COIL2, D1.cathode
  N4: Componente1.PWM_D6, BC547.0
  N5: LED1.anode, R1.Pin_0
  N6: U1.COIL1, D1.anode, BC547.1
